# Fritzing sketch AirQuality (saved by Fritzing 0.9.3b)
circuit board: 8cm x 6cm
breadboards: 1

parts:
  Display1 = rounded female pin header, 4 pins [form="♀ (female rounded)"]
  BMD180 = female pin header, 4 pins [form="♀ (female)"]
  DHT11 = rounded female pin header, 3 pins [form="♀ (female rounded)"]
  Photoresistor = rounded female pin header, 3 pins [form="♀ (female rounded)"]
  MQ135 = female pin header, 4 pins [form="♀ (female)"]
  MQ7 = female pin header, 4 pins [form="♀ (female)"]
  MQ3 = female pin header, 4 pins [form="♀ (female)"]
  Power_plug = Power plug
  SW2 = ENCODER_RGB_CA [package=encoder_led_3]
  R2 = Resistor [tolerance=±5% resistance=330 package=THT]
  R1 = Resistor [tolerance=±5% resistance=100 package=THT]
  Buzzer1 = Buzzer 12mm [package=buzzer-12mm-ns]
  RTC_Module1 = rounded female pin header, 5 pins [form="♀ (female rounded)"]
  ESP8266 = double row rounded female pin header, 8 pins [form="♀ (female rounded)"]
  Arduino_Nano = Arduino Nano (Rev3.0)
  R3 = Resistor [tolerance=±5% resistance=10k package=THT]
  R5 = Resistor [tolerance=±5% resistance=1k package=THT]
  R4 = Resistor [tolerance=±5% resistance=3.3k package=THT]

nets:
  N1: Display1.pin1, BMD180.pin2, Arduino_Nano.A5
  N2: Display1.pin2, BMD180.pin1, Arduino_Nano.A4
  N3: Display1.pin3, DHT11.pin2, Photoresistor.pin2, MQ135.pin1, MQ7.pin1, MQ3.pin1, RTC_Module1.pin1, Arduino_Nano.5V
  GND: Display1.pin4, BMD180.pin3, DHT11.pin3, Photoresistor.pin3, MQ135.pin2, MQ7.pin2, MQ3.pin2, Power_plug.GND, SW2.+, SW2.C, Buzzer1.1, RTC_Module1.pin2, ESP8266.pin8, Arduino_Nano.GND, R4.Pin_1
  N4: BMD180.pin4, ESP8266.pin2, Arduino_Nano.3V3, R3.Pin_1
  N5: DHT11.pin1, Arduino_Nano.D2
  N6: Photoresistor.pin1, Arduino_Nano.A0
  N7: MQ135.pin4, Arduino_Nano.A1
  N8: MQ7.pin4, Arduino_Nano.A2
  N9: MQ3.pin4, Arduino_Nano.A3
  VCC: Power_plug.VCC, Arduino_Nano.VIN
  N10: SW2.SW, R2.Pin_1
  N11: SW2.A, Arduino_Nano.D4
  N12: SW2.B, Arduino_Nano.D3
  N13: R2.Pin_0, Arduino_Nano.D9
  N14: R1.Pin_0, Arduino_Nano.D8
  N15: R1.Pin_1, Buzzer1.2
  N16: RTC_Module1.pin3, Arduino_Nano.D5
  N17: RTC_Module1.pin4, Arduino_Nano.D6
  N18: RTC_Module1.pin5, Arduino_Nano.D7
  N19: ESP8266.pin1, Arduino_Nano.D1/TX
  N20: ESP8266.pin4, R3.Pin_0
  N21: ESP8266.pin5, R5.Pin_0
  N22: Arduino_Nano.D0/RX, R5.Pin_1, R4.Pin_0

notes:
  Made by Koni 2018
  konrad.heimel@gmail.com
